// Logisim project SyzygyA100.circ as structural Verilog
module Full_Adder__x1 (
  input  in_1,
  input  in_2,
  input  in_3,
  output out_4,
  output out_5
);

  wire and_1_out, and_2_out, xor_1_out;

  and and_1 (and_1_out, in_2, in_3);
  xor xor_1 (xor_1_out, in_2, in_3);
  or or_1 (out_5, and_1_out, and_2_out);
  and and_2 (and_2_out, xor_1_out, in_1);
  xor xor_2 (out_4, xor_1_out, in_1);
endmodule

module Full_Adder__x8 (
  input  [7:0] in_1,
  input  in_2,
  input  [7:0] in_3,
  output [7:0] out_4,
  output out_5
);

  wire full_adder_x1_1_out_5, full_adder_x1_2_out_5, full_adder_x1_3_out_5, full_adder_x1_4_out_5,
       full_adder_x1_5_out_5, full_adder_x1_6_out_5, full_adder_x1_7_out_5;

  Full_Adder__x1 full_adder_x1_1 (
    .in_2(in_3[0]), .in_3(in_1[0]), .out_4(out_4[0]), .in_1(in_2), .out_5(full_adder_x1_1_out_5));
  Full_Adder__x1 full_adder_x1_2 (
    .in_2(in_3[1]), .in_3(in_1[1]), .out_4(out_4[1]), .in_1(full_adder_x1_1_out_5),
    .out_5(full_adder_x1_2_out_5));
  Full_Adder__x1 full_adder_x1_3 (
    .in_2(in_3[2]), .in_3(in_1[2]), .out_4(out_4[2]), .in_1(full_adder_x1_2_out_5),
    .out_5(full_adder_x1_3_out_5));
  Full_Adder__x1 full_adder_x1_4 (
    .in_2(in_3[3]), .in_3(in_1[3]), .out_4(out_4[3]), .in_1(full_adder_x1_3_out_5),
    .out_5(full_adder_x1_4_out_5));
  Full_Adder__x1 full_adder_x1_5 (
    .in_2(in_3[4]), .in_3(in_1[4]), .out_4(out_4[4]), .in_1(full_adder_x1_4_out_5),
    .out_5(full_adder_x1_5_out_5));
  Full_Adder__x1 full_adder_x1_6 (
    .in_2(in_3[5]), .in_3(in_1[5]), .out_4(out_4[5]), .in_1(full_adder_x1_5_out_5),
    .out_5(full_adder_x1_6_out_5));
  Full_Adder__x1 full_adder_x1_7 (
    .in_2(in_3[6]), .in_3(in_1[6]), .out_4(out_4[6]), .in_1(full_adder_x1_6_out_5),
    .out_5(full_adder_x1_7_out_5));
  Full_Adder__x1 full_adder_x1_8 (
    .in_2(in_3[7]), .in_3(in_1[7]), .out_4(out_4[7]), .in_1(full_adder_x1_7_out_5), .out_5(out_5));
endmodule

module And__x8 (
  input  [7:0] in_1,
  input  [7:0] in_2,
  output [7:0] out_3
);

  and and_1 (out_3[0], in_1[0], in_2[0]);
  and and_2 (out_3[1], in_1[1], in_2[1]);
  and and_3 (out_3[2], in_1[2], in_2[2]);
  and and_4 (out_3[3], in_1[3], in_2[3]);
  and and_5 (out_3[4], in_1[4], in_2[4]);
  and and_6 (out_3[5], in_1[5], in_2[5]);
  and and_7 (out_3[6], in_1[6], in_2[6]);
  and and_8 (out_3[7], in_1[7], in_2[7]);
endmodule

module Register__x8 (
  input  in_1,
  input  [7:0] in_2,
  input  in_3,
  input  in_4,
  input  in_5,
  output [7:0] out_6
);

  wire [7:0] d_ff_1_q;

  D_Flip_Flop d_ff_1 (.clk(in_3), .D(in_2[0]), .Q(d_ff_1_q[0]), .en(in_4), .reset(in_5));  // open: Qn, preset
  D_Flip_Flop d_ff_2 (.clk(in_3), .D(in_2[1]), .Q(d_ff_1_q[1]), .en(in_4), .reset(in_5));  // open: Qn, preset
  D_Flip_Flop d_ff_3 (.clk(in_3), .D(in_2[2]), .Q(d_ff_1_q[2]), .en(in_4), .reset(in_5));  // open: Qn, preset
  D_Flip_Flop d_ff_4 (.clk(in_3), .D(in_2[3]), .Q(d_ff_1_q[3]), .en(in_4), .reset(in_5));  // open: Qn, preset
  D_Flip_Flop d_ff_5 (.clk(in_3), .D(in_2[4]), .Q(d_ff_1_q[4]), .en(in_4), .reset(in_5));  // open: Qn, preset
  D_Flip_Flop d_ff_6 (.clk(in_3), .D(in_2[5]), .Q(d_ff_1_q[5]), .en(in_4), .reset(in_5));  // open: Qn, preset
  D_Flip_Flop d_ff_7 (.clk(in_3), .D(in_2[6]), .Q(d_ff_1_q[6]), .en(in_4), .reset(in_5));  // open: Qn, preset
  D_Flip_Flop d_ff_8 (.clk(in_3), .D(in_2[7]), .Q(d_ff_1_q[7]), .en(in_4), .reset(in_5));  // open: Qn, preset
  Buffer__x8 buffer_x8_1 (.in_1(d_ff_1_q), .out_3(out_6), .in_2(in_1));
endmodule

module Buffer__x8 (
  input  [7:0] in_1,
  input  in_2,
  output [7:0] out_3
);

  and and_1 (out_3[0], in_1[0], in_2);
  and and_2 (out_3[1], in_1[1], in_2);
  and and_3 (out_3[2], in_1[2], in_2);
  and and_4 (out_3[3], in_1[3], in_2);
  and and_5 (out_3[4], in_1[4], in_2);
  and and_6 (out_3[5], in_1[5], in_2);
  and and_7 (out_3[6], in_1[6], in_2);
  and and_8 (out_3[7], in_1[7], in_2);
endmodule
